# Fritzing sketch led_clock_fritzing (saved by Fritzing 1.0.4)

parts:
  U1 = WS2812 RGB LED strip
  U2 = ESP8266 NodeMCU LoLin module
  JACK1 = 2.1mm Barrel Jack with Terminal Block

nets:
  GND: U1.GND, U2.GND, JACK1.NEG
  N1: U1.VCC, U2.VU
  N2: U1.DIN, U2.D2
  N3: U2.Vin, JACK1.POS

notes:
  58 LEDs WS2812E 5V
  DC 5V 2A Power Supply
  NodeMCU v0.9 ESP8266

custom parts:
  WS2812 RGB LED strip: WS2812 strip
  ESP8266 NodeMCU LoLin module: ESP8266 based NodeMCU
